# Fritzing sketch BE-SAP-1-ArduinoMegaProgramLoader (saved by Fritzing 0.9.4)
breadboards: 1

parts:
  Part1 = Arduino Mega 2560 (Rev3)
  S1 = Pushbutton [package="[SMD]"]
  SW1 = DIP Switch 8 Position [package=dipswitch-08]
  SW2 = DIP Switch 4 Position [package=dipswitch-04]

nets:
  N1: Part1.D22, SW2.1
  N2: Part1.D24, SW2.2
  N3: Part1.D26, SW2.3
  N4: Part1.D28, SW2.4
  N5: Part1.D32, S1.Pin_1, S1.Pin_2
  N6: Part1.D37, SW1.1
  N7: Part1.D39, SW1.2
  N8: Part1.D41, SW1.3
  N9: Part1.D43, SW1.4
  N10: Part1.D45, SW1.5
  N11: Part1.D47, SW1.6
  N12: Part1.D49, SW1.7
  N13: Part1.D51, SW1.8
  N14: Part1.GND, S1.Pin_3, S1.Pin_4
  N15: SW1.9, SW1.10, SW1.11, SW1.12, SW1.13, SW1.14, SW1.15, SW1.16, SW2.5, SW2.6, SW2.7, SW2.8

notes:
  Address Dip Switches
  Hook up leads to Arduino on the same side as the Green lines that go to the 74LS157 (opposite side as ground)
  Ensure all are on OFF Position when loading programs from Arduino)
  Data Dip Switches
  Hook up leads to Arduino on the same side as the Green lines that go to the the 74LS157s (opposite side as ground)
  Ensure all are on OFF Position when loading programs from Arduino)
  Write Button
  Hook up the Write Button on the same line as the as the yellow lead going into the adjacent 74LS157 This line will be "strobed" every time the Arduino is ready to write to RAM
